// Logisim project pj2_JoaoMaciel147.circ as structural Verilog: 1 circuit, main circuit main
module main (
  input  [3:0] add_001x,
  input  [3:0] and_100x,
  output out_3,
  output out_4
);

  wire ALU_OP, ALU_SRC, CLK, registerfile_1_p7;
  wire [3:0] mips_alu_1_p3;
  wire [4:0] multiplexer_1_out;
  wire [31:0] adder_1_out, bit_extender_1_out, mips_alu_1_p4, mips_ram_1_p6, mipsprogramrom_1_p2,
       multiplexer_2_out, register_1_q, registerfile_1_p1, registerfile_1_p8;

  Adder #(.width(32)) adder_1 (.a(register_1_q), .b(32'h4), .out(adder_1_out));  // open: cin, cout
  Register #(.width(32)) register_1 (.D(adder_1_out), .Q(register_1_q), .clk(CLK));  // open: en, clr
  // MIPSProgramROM mipsprogramrom_1: pin names not known; wires that end beside it: register_1_q, mipsprogramrom_1_p2
  Multiplexer #(.width(5)) multiplexer_1 (
    .in0(mipsprogramrom_1_p2[15:11]), .in1(mipsprogramrom_1_p2[20:16]), .out(multiplexer_1_out), .sel(ALU_SRC));  // open: en
  and ADDIU (out_3, mipsprogramrom_1_p2[26], ~mipsprogramrom_1_p2[27], ~mipsprogramrom_1_p2[28], mipsprogramrom_1_p2[29], ~mipsprogramrom_1_p2[30], ~mipsprogramrom_1_p2[31]);  // AND_Gate
  and ANDI (out_4, ~mipsprogramrom_1_p2[26], ~mipsprogramrom_1_p2[27], mipsprogramrom_1_p2[28], mipsprogramrom_1_p2[29], ~mipsprogramrom_1_p2[30], ~mipsprogramrom_1_p2[31]);  // AND_Gate
  assign bit_extender_1_out = {{16{1'b0}}, mipsprogramrom_1_p2[15:0]};  // Bit_Extender bit_extender_1
  // RegisterFile registerfile_1: pin names not known; wires that end beside it: registerfile_1_p1, CLK, ALU_SRC, multiplexer_1_out, mipsprogramrom_1_p2[25:21], mipsprogramrom_1_p2[20:16], registerfile_1_p7, registerfile_1_p8
  Multiplexer #(.width(32)) multiplexer_2 (
    .in0(registerfile_1_p8), .in1(bit_extender_1_out), .out(multiplexer_2_out), .sel(ALU_SRC));  // open: en
  // Mips_ALU mips_alu_1: pin names not known; wires that end beside it: registerfile_1_p7, multiplexer_2_out, mips_alu_1_p3, mips_alu_1_p4
  Multiplexer #(.width(4), .enable("false")) multiplexer_3 (
    .in0(add_001x), .in1(and_100x), .out(mips_alu_1_p3), .sel(ALU_OP));
  or or_1 (ALU_SRC, out_3, out_4);
  not not_1 (ALU_OP, out_3);
  // MIPS_RAM mips_ram_1: pin names not known; wires that end beside it: mips_alu_1_p4[19:0], registerfile_1_p8, 1'b0, CLK, 1'b0, mips_ram_1_p6
  Multiplexer #(.width(32), .enable("false")) multiplexer_4 (
    .in0(mips_alu_1_p4), .in1(mips_ram_1_p6), .out(registerfile_1_p1), .sel(1'b0));
  Clock clock_1 (.out(CLK));

  // Other names for the same wires on the sheet: REG_DEST = ALU_SRC; REG_W = ALU_SRC

  // Notes on the sheet:
  //   MEMÓRIA DE PROGRAMA
  //   R
  //   I
  //   VAZIO
  //   VAZIO
endmodule
